# Fritzing sketch Pong (saved by Fritzing 0.9.3b)
breadboards: 1

parts:
  J1 = double row male pin header, 4 pins [form="♂ (male)"]
  Part1 = Arduino Uno (Rev3) - ICSP
  Power_plug1 = Power plug
  S1 = Pushbutton [package="[THT]"]
  S2 = Pushbutton [package="[THT]"]
  S3 = Pushbutton [package="[THT]"]
  S4 = Pushbutton [package="[THT]"]
  R1 = Resistor [tolerance=±5% resistance=220 package=THT]
  R2 = Resistor [tolerance=±5% resistance=220 package=THT]
  R3 = Resistor [tolerance=±5% resistance=220 package=THT]
  R4 = Resistor [tolerance=±5% resistance=220 package=THT]

nets:
  N1: J1.pin1, Part1.GND
  N2: J1.pin2, Part1.3V3
  N3: J1.pin3, Part1.A5/SCL
  N4: J1.pin4, Part1.A4/SDA
  N5: Part1.D8, S2.Pin_1, S2.Pin_2, R2.Pin_1
  N6: Part1.D9_PWM, S1.Pin_1, S1.Pin_2, R1.Pin_1
  N7: Part1.D2, S4.Pin_1, S4.Pin_2, R3.Pin_1
  N8: Part1.D3_PWM, S3.Pin_1, S3.Pin_2, R4.Pin_1
  N9: Power_plug1.VCC, S1.Pin_3, S1.Pin_4, S2.Pin_3, S2.Pin_4, S3.Pin_3, S3.Pin_4, S4.Pin_3, S4.Pin_4
  N10: Power_plug1.GND, R1.Pin_0, R2.Pin_0, R3.Pin_0, R4.Pin_0

notes:
  GND
  VCC
  SCL
  SDA
